// Logisim project secuenciales.circ as structural Verilog: 6 circuits, main circuit Flip-Flop SR
module Flip_Flop_SR (
  input  S,
  input  R,
  output Q,
  output Q_prime
);

  wire not_1_out, not_2_out;

  not not_1 (not_1_out, S);
  not not_2 (not_2_out, R);
  nand nand_1 (Q, not_1_out, Q_prime);
  nand nand_2 (Q_prime, Q, not_2_out);
endmodule

// SR W/Clock
module Flip_Flop_SR_w_Clock (
  input  S,
  input  Pulsador,
  input  R,
  output Q,
  output Q_prime
);

  wire nand_1_out, nand_2_out;

  nand nand_1 (nand_1_out, S, Pulsador);
  nand nand_2 (nand_2_out, Pulsador, R);
  nand nand_3 (Q, nand_1_out, Q_prime);
  nand nand_4 (Q_prime, Q, nand_2_out);
endmodule

module Flip_Flop_D (
  input  Set,
  input  D,
  input  Pulsador,
  input  Reset,
  output Q,
  output Q_prime
);

  wire nand_1_out, nand_2_out, nor_1_out, nor_2_out, not_1_out, not_2_out, not_3_out;

  not not_1 (not_1_out, D);
  nand nand_1 (nand_1_out, D, Pulsador);
  not not_2 (not_2_out, nand_1_out);
  nand nand_2 (nand_2_out, Pulsador, not_1_out);
  not not_3 (not_3_out, nand_2_out);
  nor nor_1 (nor_1_out, Set, not_2_out);
  nor nor_2 (nor_2_out, not_3_out, Reset);
  nand nand_3 (Q, nor_1_out, Q_prime);
  nand nand_4 (Q_prime, Q, nor_2_out);
endmodule

module Flip_Flop_JK (
  input  J,
  input  Clock,
  input  K,
  output Q,
  output Q_prime
);

  wire and_1_out, and_2_out;

  and and_1 (and_1_out, Q_prime, J);
  Flip_Flop_SR_w_Clock ff_sr_w_clock_1 (.S(and_1_out), .Q(Q_prime), .Q_prime(Q), .R(and_2_out), .Pulsador(Clock));
  and and_2 (and_2_out, K, Q);
endmodule

module reg3bHI_z (
  input  Set,
  input  e2,
  input  e1,
  input  e0,
  input  Clock,
  input  W_Enable,
  input  Enable_Out,
  input  Reset,
  output s2,
  output s1,
  output s0
);

  wire and_1_out, Flip_Flop_D_2_q, Flip_Flop_D_3_q, Flip_Flop_D_q;

  and and_1 (and_1_out, Clock, W_Enable);
  Flip_Flop_D Flip_Flop_D (.D(e2), .Set(Set), .Q(Flip_Flop_D_q), .Pulsador(and_1_out), .Reset(Reset));  // open: Q_prime
  Flip_Flop_D Flip_Flop_D_2 (
    .D(e1), .Set(Set), .Q(Flip_Flop_D_2_q), .Pulsador(and_1_out), .Reset(Reset));  // open: Q_prime
  Flip_Flop_D Flip_Flop_D_3 (
    .D(e0), .Set(Set), .Q(Flip_Flop_D_3_q), .Pulsador(and_1_out), .Reset(Reset));  // open: Q_prime
  assign s0 = Enable_Out ? Flip_Flop_D_3_q : 1'bz;  // Controlled_Buffer controlled_buffer_1
  assign s2 = Enable_Out ? Flip_Flop_D_q : 1'bz;  // Controlled_Buffer controlled_buffer_2
  assign s1 = Enable_Out ? Flip_Flop_D_2_q : 1'bz;  // Controlled_Buffer controlled_buffer_3
endmodule

module reg3b_IO (
  input  W_Enable,
  input  Reset,
  input  Enable_Out,
  output s2,
  output s1,
  output s0
);

  wire clock_1_out;

  Clock clock_1 (.out(clock_1_out));
  reg3bHI_z reg3bhi_z_1 (
    .e2(s2), .e1(s1), .e0(s0), .W_Enable(W_Enable), .s2(s2), .s1(s1), .s0(s0), .Reset(Reset),
    .Enable_Out(Enable_Out), .Clock(clock_1_out));  // open: Set
endmodule
