// Logisim project TallerLogica-Combinatorios.circ as structural Verilog: 13 circuits, main circuit sumador_simple
module sumador_simple (
  input  a,
  input  b,
  output S,
  output Cout
);

  \xor  XOR (.A(a), .B(b), .Res(S));
  and and_1 (Cout, a, b);
endmodule

module sumador_completo (
  input  Cin,
  input  A,
  input  B,
  output S,
  output Cout
);

  wire and_1_out, and_2_out, XOR_res;

  \xor  XOR (.A(A), .B(B), .Res(XOR_res));
  and and_1 (and_1_out, A, B);
  and and_2 (and_2_out, Cin, XOR_res);
  \xor  xor_2 (.A(Cin), .B(XOR_res), .Res(S));
  or or_1 (Cout, and_2_out, and_1_out);
endmodule

module sumador_4 (
  input  Cin,
  input  [3:0] A,
  input  [3:0] B,
  output [3:0] S,
  output Cout,
  output Carry_MSB
);

  wire Full_Adder_2_cout, Full_Adder_cout;

  sumador_completo Full_Adder (.A(A[0]), .B(B[0]), .Cin(Cin), .S(S[0]), .Cout(Full_Adder_cout));
  sumador_completo Full_Adder_2 (.A(A[1]), .B(B[1]), .Cin(Full_Adder_cout), .S(S[1]), .Cout(Full_Adder_2_cout));
  sumador_completo Full_Adder_3 (.A(A[2]), .B(B[2]), .Cin(Full_Adder_2_cout), .S(S[2]), .Cout(Carry_MSB));
  sumador_completo Full_Adder_4 (.A(A[3]), .B(B[3]), .Cin(Carry_MSB), .S(S[3]), .Cout(Cout));
  Hex_Digit_Display hex_digit_display_1 (.value(S));  // open: dp
endmodule

module comparador_cero (
  input  [3:0] A,
  output Z
);

  wire and_1_out, and_2_out, not_1_out, not_2_out, not_3_out, not_4_out;

  not not_1 (not_1_out, A[0]);
  not not_2 (not_2_out, A[1]);
  not not_3 (not_3_out, A[2]);
  not not_4 (not_4_out, A[3]);
  and and_1 (and_1_out, not_1_out, not_2_out);
  and and_2 (and_2_out, not_3_out, not_4_out);
  and and_3 (Z, and_1_out, and_2_out);
endmodule

module sumador_flags (
  input  Cin,
  input  [3:0] A,
  input  [3:0] B,
  output [3:0] S,
  output N,
  output Z,
  output V,
  output C
);

  wire _4Bit_Adder_carry_msb;

  sumador_4 _4Bit_Adder (.Cin(Cin), .A(A), .S({N, S[2:0]}), .B(B), .Cout(C), .Carry_MSB(_4Bit_Adder_carry_msb));
  \xor  XOR (.A(_4Bit_Adder_carry_msb), .B(C), .Res(V));
  Hex_Digit_Display hex_digit_display_1 (.value({N, S[2:0]}));  // open: dp
  comparador_cero _0 (.A({N, S[2:0]}), .Z(Z));

  assign S[3] = N;
endmodule

module incrementador_4 (
  input  [3:0] A,
  output [3:0] S
);

  sumador_4 Sum_4 (.Cin(1'b0), .A(A), .S(S), .B(4'b0001));  // open: Cout, Carry_MSB
  Hex_Digit_Display hex_digit_display_1 (.value(S));  // open: dp
endmodule

module inversor_4 (
  input  [3:0] A,
  input  INV,
  output [3:0] S
);

  wire and_1_out, and_2_out, not_4_out, not_5_out, or_1_out, or_2_out, xor_2_res, XOR_3_res, XOR_res;
  wire [2:0] not_1_out;
  wire [3:0] Incr_4B_s;

  not not_1 (not_1_out[0], A[0]);
  not not_2 (not_1_out[1], A[1]);
  not not_3 (not_1_out[2], A[2]);
  \xor  XOR (.A(A[3]), .B(A[2]), .Res(XOR_res));
  \xor  xor_2 (.A(A[3]), .B(A[1]), .Res(xor_2_res));
  \xor  XOR_3 (.A(A[3]), .B(A[0]), .Res(XOR_3_res));
  incrementador_4 Incr_4B (.A({A[3], not_1_out}), .S(Incr_4B_s));
  not not_4 (not_4_out, A[3]);
  and and_1 (and_1_out, XOR_res, xor_2_res);
  Multiplexer #(.width(4), .enable("false")) multiplexer_1 (.in0(Incr_4B_s), .in1(A), .out(S), .sel(or_1_out));
  or or_1 (or_1_out, or_2_out, not_5_out);
  or or_2 (or_2_out, not_4_out, and_2_out);
  not not_5 (not_5_out, INV);
  and and_2 (and_2_out, and_1_out, XOR_3_res);
  Hex_Digit_Display hex_digit_display_1 (.value(S));  // open: dp
endmodule

module ALU (
  input  Cin,
  input  [3:0] A,
  input  [3:0] B,
  input  [1:0] OP,
  output [3:0] S,
  output N,
  output Z,
  output V,
  output C
);

  wire not_1_out, Resta_c, Resta_n, Resta_v, Resta_z, Sumador_c, Sumador_n, Sumador_v, Sumador_z;
  wire [3:0] ANDs_s, Inv_s, ORs_s, Resta_s, Sumador_s;

  sumador_flags Sumador (
    .A(A), .B(B), .Cin(Cin), .S(Sumador_s), .N(Sumador_n), .Z(Sumador_z), .V(Sumador_v), .C(Sumador_c));
  sumador_flags Resta (.A(A), .B(Inv_s), .Cin(Cin), .S(Resta_s), .N(Resta_n), .Z(Resta_z), .V(Resta_v), .C(Resta_c));
  inv4_v2 Inv (.A(B), .INV(1'b1), .S(Inv_s));
  borrow borrow_1 (.A(A), .B(B));  // open: out_3
  bandb ANDs (.A(A), .B(B), .S(ANDs_s));
  borb ORs (.A(A), .B(B), .S(ORs_s));
  not not_1 (not_1_out, Resta_c);
  Multiplexer #(.select(2), .width(4), .enable("false")) multiplexer_1 (
    .in0(Sumador_s), .in1(Resta_s), .in2(ANDs_s), .in3(ORs_s), .out(S), .sel(OP));
  Hex_Digit_Display hex_digit_display_1 (.value(S));  // open: dp
  Multiplexer #(.select(2), .enable("false")) multiplexer_2 (
    .in0(Sumador_n), .in1(Resta_n), .in2(Sumador_n), .in3(Sumador_n), .out(N), .sel(OP));
  Multiplexer #(.select(2), .enable("false")) multiplexer_3 (
    .in0(Sumador_z), .in1(Resta_z), .in2(Sumador_z), .in3(Sumador_z), .out(Z), .sel(OP));
  Multiplexer #(.select(2), .enable("false")) multiplexer_4 (
    .in0(Sumador_v), .in1(Resta_v), .in2(Sumador_v), .in3(Sumador_v), .out(V), .sel(OP));
  Multiplexer #(.select(2), .enable("false")) multiplexer_5 (
    .in0(Sumador_c), .in1(not_1_out), .in2(Sumador_c), .in3(Sumador_c), .out(C), .sel(OP));
endmodule

module \xor  (
  input  A,
  input  B,
  output Res
);

  wire and_1_out, and_2_out, not_1_out, not_2_out;

  not not_1 (not_1_out, A);
  not not_2 (not_2_out, B);
  and and_1 (and_1_out, not_1_out, B);
  and and_2 (and_2_out, A, not_2_out);
  or or_1 (Res, and_1_out, and_2_out);
endmodule

module bandb (
  input  [3:0] A,
  input  [3:0] B,
  output [3:0] S
);

  and and_1 (S[0], A[0], B[0]);
  and and_2 (S[1], A[1], B[1]);
  and and_3 (S[2], A[2], B[2]);
  and and_4 (S[3], A[3], B[3]);
endmodule

module borb (
  input  [3:0] A,
  input  [3:0] B,
  output [3:0] S
);

  or or_1 (S[0], A[0], B[0]);
  or or_2 (S[1], A[1], B[1]);
  or or_3 (S[2], A[2], B[2]);
  or or_4 (S[3], A[3], B[3]);
endmodule

module inv4_v2 (
  input  [3:0] A,
  input  INV,
  output [3:0] S
);

  wire not_5_out;
  wire [3:0] Incr_s, not_1_out;

  not not_1 (not_1_out[0], A[0]);
  not not_2 (not_1_out[1], A[1]);
  not not_3 (not_1_out[2], A[2]);
  not not_4 (not_1_out[3], A[3]);
  incrementador_4 Incr (.A(not_1_out), .S(Incr_s));
  Multiplexer #(.width(4), .enable("false")) multiplexer_1 (.in0(Incr_s), .in1(A), .out(S), .sel(not_5_out));
  not not_5 (not_5_out, INV);
  Hex_Digit_Display hex_digit_display_1 (.value(S));  // open: dp
endmodule

module borrow (
  input  [3:0] A,
  input  [3:0] B,
  output out_3
);

  wire a0_b0_out, a1_b1_out, a2_b2_out, a3_b3_out, and_1_out, and_2_out, and_3_out, and_4_out, and_5_out,
       and_6_out, not_1_out, not_2_out, not_3_out, not_4_out, not_5_out, not_6_out, not_7_out, not_8_out,
       not_9_out, not_10_out, or_1_out, or_2_out;

  not not_1 (not_1_out, A[3]);
  not not_2 (not_2_out, A[2]);
  not not_3 (not_3_out, A[1]);
  not not_4 (not_4_out, A[0]);
  and a3_b3 (a3_b3_out, not_1_out, B[3]);
  not not_5 (not_5_out, a3_b3_out);
  and a2_b2 (a2_b2_out, not_2_out, B[2]);
  and and_1 (and_1_out, not_5_out, a2_b2_out);
  not not_6 (not_6_out, a3_b3_out);
  and and_2 (and_2_out, not_6_out, not_7_out);
  not not_7 (not_7_out, and_1_out);
  and a1_b1 (a1_b1_out, not_3_out, B[1]);
  or or_1 (or_1_out, a3_b3_out, and_1_out);
  and and_3 (and_3_out, and_2_out, a1_b1_out);
  not not_8 (not_8_out, a3_b3_out);
  and and_4 (and_4_out, not_8_out, not_9_out);
  not not_9 (not_9_out, a2_b2_out);
  not not_10 (not_10_out, a1_b1_out);
  or or_2 (or_2_out, or_1_out, and_3_out);
  and and_5 (and_5_out, and_4_out, not_10_out);
  and a0_b0 (a0_b0_out, not_4_out, B[0]);
  and and_6 (and_6_out, and_5_out, a0_b0_out);
  or or_3 (out_3, or_2_out, and_6_out);
endmodule
