// Logisim project ej6.circ as structural Verilog: 1 circuit, main circuit main
module main (
  input  [7:0] A,
  input  [7:0] B,
  output [7:0] out_3
);


  assign out_3 = {B[1], A[6], B[3], A[4], B[5], A[2], B[7], A[0]};
endmodule
